// Logisim project cpu.circ as structural Verilog: 3 circuits, main circuit main
module main (
);

  wire clock_1_out, dipswitch_1_sw7, dipswitch_1_sw8, instruction_spliter_1_out_6,
       instruction_spliter_1_out_7, instruction_spliter_1_out_8, instruction_spliter_1_out_9,
       instruction_spliter_1_out_10, instruction_spliter_1_out_11, instruction_spliter_1_out_12,
       instruction_spliter_1_out_13, instruction_spliter_1_out_14, instruction_spliter_1_out_15,
       instruction_spliter_1_out_16, instruction_spliter_1_out_17, instruction_spliter_1_out_18,
       instruction_spliter_1_out_19, instruction_spliter_1_out_20, instruction_spliter_1_out_21,
       instruction_spliter_1_out_22, instruction_spliter_1_out_23, instruction_spliter_1_out_24,
       instruction_spliter_1_out_25, instruction_spliter_1_out_26, instruction_spliter_1_out_27,
       instruction_spliter_1_out_28, instruction_spliter_1_out_29, instruction_spliter_1_out_30,
       instruction_spliter_1_out_31, instruction_spliter_1_out_32, instruction_spliter_1_out_33,
       instruction_spliter_1_out_34, instruction_spliter_1_out_35, instruction_spliter_1_out_36,
       instruction_spliter_1_out_37, instruction_spliter_1_out_38, instruction_spliter_1_out_39,
       instruction_spliter_1_out_40, instruction_spliter_1_out_41, instruction_spliter_1_out_42,
       instruction_spliter_1_out_43, instruction_spliter_1_out_44, instruction_spliter_1_out_45,
       instruction_spliter_1_out_46, instruction_spliter_1_out_47, instruction_spliter_1_out_48,
       instruction_spliter_1_out_49, instruction_spliter_1_out_50, instruction_spliter_1_out_51,
       instruction_spliter_1_out_52, instruction_spliter_1_out_53, instruction_spliter_1_out_54,
       instruction_spliter_1_out_55, instruction_spliter_1_out_56, instruction_spliter_1_out_57,
       instruction_spliter_1_out_58, instruction_spliter_1_out_59, instruction_spliter_1_out_60,
       instruction_spliter_1_out_61, instruction_spliter_1_out_62, instruction_spliter_1_out_63,
       instruction_spliter_1_out_64, instruction_spliter_1_out_65;
  wire [7:0] counter_1_q, instruction_spliter_1_out_address, instruction_spliter_1_out_data_h,
       instruction_spliter_1_out_data_l;
  wire [15:0] instruction_spliter_1_out_data;
  wire [39:0] rom_1_data;

  ROM #(.dataWidth(40)) rom_1 (.addr(counter_1_q), .data(rom_1_data));
  DipSwitch dipswitch_1 (.sw7(dipswitch_1_sw7), .sw8(dipswitch_1_sw8));  // open: sw1, sw2, sw3, sw4, sw5, sw6
  Counter counter_1 (
    .clr(dipswitch_1_sw7), .up(1'b1), .count(dipswitch_1_sw8), .clk(clock_1_out), .Q(counter_1_q));  // open: load, D, carry
  Clock clock_1 (.out(clock_1_out));
  Instruction_Spliter instruction_spliter_1 (
    .Input_Data(rom_1_data), .Out_Data(instruction_spliter_1_out_data),
    .Out_Data_H(instruction_spliter_1_out_data_h), .Out_Data_L(instruction_spliter_1_out_data_l),
    .Out_Address(instruction_spliter_1_out_address), .out_6(instruction_spliter_1_out_6),
    .out_7(instruction_spliter_1_out_7), .out_8(instruction_spliter_1_out_8),
    .out_9(instruction_spliter_1_out_9), .out_10(instruction_spliter_1_out_10),
    .out_11(instruction_spliter_1_out_11), .out_12(instruction_spliter_1_out_12),
    .out_13(instruction_spliter_1_out_13), .out_14(instruction_spliter_1_out_14),
    .out_15(instruction_spliter_1_out_15), .out_16(instruction_spliter_1_out_16),
    .out_17(instruction_spliter_1_out_17), .out_18(instruction_spliter_1_out_18),
    .out_19(instruction_spliter_1_out_19), .out_20(instruction_spliter_1_out_20),
    .out_21(instruction_spliter_1_out_21), .out_22(instruction_spliter_1_out_22),
    .out_23(instruction_spliter_1_out_23), .out_24(instruction_spliter_1_out_24),
    .out_25(instruction_spliter_1_out_25), .out_26(instruction_spliter_1_out_26),
    .out_27(instruction_spliter_1_out_27), .out_28(instruction_spliter_1_out_28),
    .out_29(instruction_spliter_1_out_29), .out_30(instruction_spliter_1_out_30),
    .out_31(instruction_spliter_1_out_31), .out_32(instruction_spliter_1_out_32),
    .out_33(instruction_spliter_1_out_33), .out_34(instruction_spliter_1_out_34),
    .out_35(instruction_spliter_1_out_35), .out_36(instruction_spliter_1_out_36),
    .out_37(instruction_spliter_1_out_37), .out_38(instruction_spliter_1_out_38),
    .out_39(instruction_spliter_1_out_39), .out_40(instruction_spliter_1_out_40),
    .out_41(instruction_spliter_1_out_41), .out_42(instruction_spliter_1_out_42),
    .out_43(instruction_spliter_1_out_43), .out_44(instruction_spliter_1_out_44),
    .out_45(instruction_spliter_1_out_45), .out_46(instruction_spliter_1_out_46),
    .out_47(instruction_spliter_1_out_47), .out_48(instruction_spliter_1_out_48),
    .out_49(instruction_spliter_1_out_49), .out_50(instruction_spliter_1_out_50),
    .out_51(instruction_spliter_1_out_51), .out_52(instruction_spliter_1_out_52),
    .out_53(instruction_spliter_1_out_53), .out_54(instruction_spliter_1_out_54),
    .out_55(instruction_spliter_1_out_55), .out_56(instruction_spliter_1_out_56),
    .out_57(instruction_spliter_1_out_57), .out_58(instruction_spliter_1_out_58),
    .out_59(instruction_spliter_1_out_59), .out_60(instruction_spliter_1_out_60),
    .out_61(instruction_spliter_1_out_61), .out_62(instruction_spliter_1_out_62),
    .out_63(instruction_spliter_1_out_63), .out_64(instruction_spliter_1_out_64),
    .out_65(instruction_spliter_1_out_65));
  // Probe on instruction_spliter_1_out_data
  // Probe on instruction_spliter_1_out_data_h
  // Probe on instruction_spliter_1_out_address
  // Probe on instruction_spliter_1_out_6
  // Probe on instruction_spliter_1_out_7
  // Probe on instruction_spliter_1_out_8
  // Probe on instruction_spliter_1_out_9
  // Probe on instruction_spliter_1_out_10
  // Probe on instruction_spliter_1_out_11
  // Probe on instruction_spliter_1_out_12
  // Probe on instruction_spliter_1_out_13
  // Probe on instruction_spliter_1_out_14
  // Probe on instruction_spliter_1_out_15
  // Probe on instruction_spliter_1_out_16
  // Probe on instruction_spliter_1_out_17
  // Probe on instruction_spliter_1_out_18
  // Probe on instruction_spliter_1_out_19
  // Probe on instruction_spliter_1_out_20
  // Probe on instruction_spliter_1_out_21
  // Probe on instruction_spliter_1_out_22
  // Probe on instruction_spliter_1_out_23
  // Probe on instruction_spliter_1_out_24
  // Probe on instruction_spliter_1_out_25
  // Probe on instruction_spliter_1_out_26
  // Probe on instruction_spliter_1_out_27
  // Probe on instruction_spliter_1_out_28
  // Probe on instruction_spliter_1_out_29
  // Probe on instruction_spliter_1_out_30
  // Probe on instruction_spliter_1_out_31
  // Probe on instruction_spliter_1_out_32
  // Probe on instruction_spliter_1_out_33
  // Probe on instruction_spliter_1_out_34
  // Probe on instruction_spliter_1_out_35
  // Probe on instruction_spliter_1_out_36
  // Probe on instruction_spliter_1_out_37
  // Probe on instruction_spliter_1_out_38
  // Probe on instruction_spliter_1_out_39
  // Probe on instruction_spliter_1_out_40
  // Probe on instruction_spliter_1_out_41
  // Probe on instruction_spliter_1_out_42
  // Probe on instruction_spliter_1_out_43
  // Probe on instruction_spliter_1_out_44
  // Probe on instruction_spliter_1_out_45
  // Probe on instruction_spliter_1_out_46
  // Probe on instruction_spliter_1_out_47
  // Probe on instruction_spliter_1_out_48
  // Probe on instruction_spliter_1_out_49
  // Probe on instruction_spliter_1_out_50
  // Probe on instruction_spliter_1_out_51
  // Probe on instruction_spliter_1_out_52
  // Probe on instruction_spliter_1_out_53
  // Probe on instruction_spliter_1_out_54
  // Probe on instruction_spliter_1_out_55
  // Probe on instruction_spliter_1_out_56
  // Probe on instruction_spliter_1_out_57
  // Probe on instruction_spliter_1_out_58
  // Probe on instruction_spliter_1_out_59
  // Probe on instruction_spliter_1_out_60
  // Probe on instruction_spliter_1_out_61
  // Probe on instruction_spliter_1_out_62
  // Probe on instruction_spliter_1_out_63
  // Probe on instruction_spliter_1_out_64
  // Probe on instruction_spliter_1_out_65
  // Probe on instruction_spliter_1_out_data_l

  // Notes on the sheet:
  //   contents of rom_1 (hex, n*v repeats v):
  //   33000004 10041 20065 42010002 fffeffffff
endmodule

module Instruction_Spliter (
  input  [39:0] Input_Data,
  output [15:0] Out_Data,
  output [7:0] Out_Data_H,
  output [7:0] Out_Data_L,
  output [7:0] Out_Address,
  output out_6,
  output out_7,
  output out_8,
  output out_9,
  output out_10,
  output out_11,
  output out_12,
  output out_13,
  output out_14,
  output out_15,
  output out_16,
  output out_17,
  output out_18,
  output out_19,
  output out_20,
  output out_21,
  output out_22,
  output out_23,
  output out_24,
  output out_25,
  output out_26,
  output out_27,
  output out_28,
  output out_29,
  output out_30,
  output out_31,
  output out_32,
  output out_33,
  output out_34,
  output out_35,
  output out_36,
  output out_37,
  output out_38,
  output out_39,
  output out_40,
  output out_41,
  output out_42,
  output out_43,
  output out_44,
  output out_45,
  output out_46,
  output out_47,
  output out_48,
  output out_49,
  output out_50,
  output out_51,
  output out_52,
  output out_53,
  output out_54,
  output out_55,
  output out_56,
  output out_57,
  output out_58,
  output out_59,
  output out_60,
  output out_61,
  output out_62,
  output out_63,
  output out_64,
  output out_65
);

  wire decoder16_1_out_63;

  // Probe on Input_Data[39:24]
  decoder16 decoder16_1 (
    .Data(Input_Data[39:24]), .Enable(1'b1), .out_3(out_6), .out_4(out_7), .out_5(out_8), .out_6(out_9),
    .out_7(out_10), .out_8(out_11), .out_9(out_12), .out_10(out_13), .out_11(out_14), .out_12(out_15),
    .out_13(out_16), .out_14(out_17), .out_15(out_18), .out_16(out_19), .out_17(out_20), .out_18(out_21),
    .out_19(out_22), .out_20(out_23), .out_21(out_24), .out_22(out_25), .out_23(out_26), .out_24(out_27),
    .out_25(out_28), .out_26(out_29), .out_27(out_30), .out_28(out_31), .out_29(out_32), .out_30(out_33),
    .out_31(out_34), .out_32(out_35), .out_33(out_36), .out_34(out_37), .out_35(out_38), .out_36(out_39),
    .out_37(out_40), .out_38(out_41), .out_39(out_42), .out_40(out_43), .out_41(out_44), .out_42(out_45),
    .out_43(out_46), .out_44(out_47), .out_45(out_48), .out_46(out_49), .out_47(out_50), .out_48(out_51),
    .out_49(out_52), .out_50(out_53), .out_51(out_54), .out_52(out_55), .out_53(out_56), .out_54(out_57),
    .out_55(out_58), .out_56(out_59), .out_57(out_60), .out_58(out_61), .out_59(out_62), .out_60(out_63),
    .out_61(out_64), .out_62(out_65), .out_63(decoder16_1_out_63));

  assign Out_Address = Input_Data[23:16];
  assign Out_Data = Input_Data[15:0];
  assign Out_Data_H = Input_Data[7:0];
  assign Out_Data_L = Input_Data[15:8];
endmodule

module decoder16 (
  input  [15:0] Data,
  input  Enable,
  output out_3,
  output out_4,
  output out_5,
  output out_6,
  output out_7,
  output out_8,
  output out_9,
  output out_10,
  output out_11,
  output out_12,
  output out_13,
  output out_14,
  output out_15,
  output out_16,
  output out_17,
  output out_18,
  output out_19,
  output out_20,
  output out_21,
  output out_22,
  output out_23,
  output out_24,
  output out_25,
  output out_26,
  output out_27,
  output out_28,
  output out_29,
  output out_30,
  output out_31,
  output out_32,
  output out_33,
  output out_34,
  output out_35,
  output out_36,
  output out_37,
  output out_38,
  output out_39,
  output out_40,
  output out_41,
  output out_42,
  output out_43,
  output out_44,
  output out_45,
  output out_46,
  output out_47,
  output out_48,
  output out_49,
  output out_50,
  output out_51,
  output out_52,
  output out_53,
  output out_54,
  output out_55,
  output out_56,
  output out_57,
  output out_58,
  output out_59,
  output out_60,
  output out_61,
  output out_62,
  output out_63
);

  wire decoder_1_out0, decoder_1_out1, decoder_1_out2, decoder_1_out3, decoder_1_out4, decoder_1_out5,
       decoder_1_out6, decoder_1_out7, decoder_1_out8, decoder_1_out9, decoder_1_out10, decoder_1_out11,
       decoder_1_out12, decoder_1_out13, decoder_1_out14, decoder_1_out15, decoder_2_out0, decoder_2_out1,
       decoder_2_out2, decoder_2_out3, decoder_2_out4, decoder_2_out5, decoder_2_out6, decoder_2_out7,
       decoder_2_out8, decoder_2_out9, decoder_2_out10, decoder_2_out11, decoder_2_out12, decoder_2_out13,
       decoder_2_out14, decoder_2_out15, decoder_3_out0, decoder_3_out1, decoder_3_out2, decoder_3_out3,
       decoder_3_out4, decoder_3_out5, decoder_3_out6, decoder_3_out7, decoder_3_out8, decoder_3_out9,
       decoder_3_out10, decoder_3_out11, decoder_3_out12, decoder_3_out13, decoder_3_out14, decoder_3_out15,
       decoder_4_out0, decoder_4_out1, decoder_4_out2, decoder_4_out3, decoder_4_out4, decoder_4_out5,
       decoder_4_out6, decoder_4_out7, decoder_4_out8, decoder_4_out9, decoder_4_out10, decoder_4_out11,
       decoder_4_out12, decoder_4_out13, decoder_4_out14, not_1_out, not_2_out, not_3_out, not_4_out;

  // Probe on Data[15:12]
  // Probe on Data[11:8]
  // Probe on Data[7:4]
  // Probe on Data[3:0]
  Decoder #(.select(4)) decoder_1 (
    .out0(decoder_1_out0), .out1(decoder_1_out1), .out2(decoder_1_out2), .out3(decoder_1_out3),
    .out4(decoder_1_out4), .out5(decoder_1_out5), .out6(decoder_1_out6), .out7(decoder_1_out7),
    .out8(decoder_1_out8), .out9(decoder_1_out9), .out10(decoder_1_out10), .out11(decoder_1_out11),
    .out12(decoder_1_out12), .out13(decoder_1_out13), .out14(decoder_1_out14), .out15(decoder_1_out15),
    .sel(Data[3:0]), .en(Enable));
  Decoder #(.select(4)) decoder_2 (
    .out0(decoder_2_out0), .out1(decoder_2_out1), .out2(decoder_2_out2), .out3(decoder_2_out3),
    .out4(decoder_2_out4), .out5(decoder_2_out5), .out6(decoder_2_out6), .out7(decoder_2_out7),
    .out8(decoder_2_out8), .out9(decoder_2_out9), .out10(decoder_2_out10), .out11(decoder_2_out11),
    .out12(decoder_2_out12), .out13(decoder_2_out13), .out14(decoder_2_out14), .out15(decoder_2_out15),
    .sel(Data[7:4]), .en(decoder_1_out15));
  Decoder #(.select(4)) decoder_3 (
    .out0(decoder_3_out0), .out1(decoder_3_out1), .out2(decoder_3_out2), .out3(decoder_3_out3),
    .out4(decoder_3_out4), .out5(decoder_3_out5), .out6(decoder_3_out6), .out7(decoder_3_out7),
    .out8(decoder_3_out8), .out9(decoder_3_out9), .out10(decoder_3_out10), .out11(decoder_3_out11),
    .out12(decoder_3_out12), .out13(decoder_3_out13), .out14(decoder_3_out14), .out15(decoder_3_out15),
    .sel(Data[11:8]), .en(decoder_2_out15));
  Decoder #(.select(4)) decoder_4 (
    .out0(decoder_4_out0), .out1(decoder_4_out1), .out2(decoder_4_out2), .out3(decoder_4_out3),
    .out4(decoder_4_out4), .out5(decoder_4_out5), .out6(decoder_4_out6), .out7(decoder_4_out7),
    .out8(decoder_4_out8), .out9(decoder_4_out9), .out10(decoder_4_out10), .out11(decoder_4_out11),
    .out12(decoder_4_out12), .out13(decoder_4_out13), .out14(decoder_4_out14), .out15(out_63),
    .sel(Data[15:12]), .en(decoder_3_out15));
  not not_1 (not_1_out, decoder_1_out15);
  not not_2 (not_2_out, decoder_2_out15);
  not not_3 (not_3_out, decoder_3_out15);
  not not_4 (not_4_out, out_63);
  and and_1 (out_3, decoder_1_out0, not_1_out);
  and and_2 (out_4, decoder_1_out1, not_1_out);
  and and_3 (out_5, decoder_1_out2, not_1_out);
  and and_4 (out_6, decoder_1_out3, not_1_out);
  and and_5 (out_7, decoder_1_out4, not_1_out);
  and and_6 (out_8, decoder_1_out5, not_1_out);
  and and_7 (out_9, decoder_1_out6, not_1_out);
  and and_8 (out_10, decoder_1_out7, not_1_out);
  and and_9 (out_11, decoder_1_out8, not_1_out);
  and and_10 (out_12, decoder_1_out9, not_1_out);
  and and_11 (out_13, decoder_1_out10, not_1_out);
  and and_12 (out_14, decoder_1_out11, not_1_out);
  and and_13 (out_15, decoder_1_out12, not_1_out);
  and and_14 (out_16, decoder_1_out13, not_1_out);
  and and_15 (out_17, decoder_1_out14, not_1_out);
  and and_16 (out_18, decoder_2_out0, not_2_out);
  and and_17 (out_19, decoder_2_out1, not_2_out);
  and and_18 (out_20, decoder_2_out2, not_2_out);
  and and_19 (out_21, decoder_2_out3, not_2_out);
  and and_20 (out_22, decoder_2_out4, not_2_out);
  and and_21 (out_23, decoder_2_out5, not_2_out);
  and and_22 (out_24, decoder_2_out6, not_2_out);
  and and_23 (out_25, decoder_2_out7, not_2_out);
  and and_24 (out_26, decoder_2_out8, not_2_out);
  and and_25 (out_27, decoder_2_out9, not_2_out);
  and and_26 (out_28, decoder_2_out10, not_2_out);
  and and_27 (out_29, decoder_2_out11, not_2_out);
  and and_28 (out_30, decoder_2_out12, not_2_out);
  and and_29 (out_31, decoder_2_out13, not_2_out);
  and and_30 (out_32, decoder_2_out14, not_2_out);
  and and_31 (out_33, decoder_3_out0, not_3_out);
  and and_32 (out_34, decoder_3_out1, not_3_out);
  and and_33 (out_35, decoder_3_out2, not_3_out);
  and and_34 (out_36, decoder_3_out3, not_3_out);
  and and_35 (out_37, decoder_3_out4, not_3_out);
  and and_36 (out_38, decoder_3_out5, not_3_out);
  and and_37 (out_39, decoder_3_out6, not_3_out);
  and and_38 (out_40, decoder_3_out7, not_3_out);
  and and_39 (out_41, decoder_3_out8, not_3_out);
  and and_40 (out_42, decoder_3_out9, not_3_out);
  and and_41 (out_43, decoder_3_out10, not_3_out);
  and and_42 (out_44, decoder_3_out11, not_3_out);
  and and_43 (out_45, decoder_3_out12, not_3_out);
  and and_44 (out_46, decoder_3_out13, not_3_out);
  and and_45 (out_47, decoder_3_out14, not_3_out);
  and and_46 (out_48, decoder_4_out0, not_4_out);
  and and_47 (out_49, decoder_4_out1, not_4_out);
  and and_48 (out_50, decoder_4_out2, not_4_out);
  and and_49 (out_51, decoder_4_out3, not_4_out);
  and and_50 (out_52, decoder_4_out4, not_4_out);
  and and_51 (out_53, decoder_4_out5, not_4_out);
  and and_52 (out_54, decoder_4_out6, not_4_out);
  and and_53 (out_55, decoder_4_out7, not_4_out);
  and and_54 (out_56, decoder_4_out8, not_4_out);
  and and_55 (out_57, decoder_4_out9, not_4_out);
  and and_56 (out_58, decoder_4_out10, not_4_out);
  and and_57 (out_59, decoder_4_out11, not_4_out);
  and and_58 (out_60, decoder_4_out12, not_4_out);
  and and_59 (out_61, decoder_4_out13, not_4_out);
  and and_60 (out_62, decoder_4_out14, not_4_out);
endmodule
